// Logisim project additionneur4bits.circ as structural Verilog: 1 circuit, main circuit main
module main (
  input  Cin,
  input  [3:0] a,
  input  [3:0] b,
  output [3:0] S,
  output Cout
);

  wire add1bit_1_p5, add1bit_2_p5, add1bit_3_p5;

  // add1bit_main add1bit_1: pin names not known; wires that end beside it: a[0], b[0], Cin, S[0], add1bit_1_p5
  // add1bit_main add1bit_2: pin names not known; wires that end beside it: a[1], b[1], add1bit_1_p5, S[1], add1bit_2_p5
  // add1bit_main add1bit_3: pin names not known; wires that end beside it: a[2], b[2], add1bit_2_p5, S[2], add1bit_3_p5
  // add1bit_main add1bit_4: pin names not known; wires that end beside it: a[3], b[3], add1bit_3_p5, S[3], Cout
endmodule
