// Logisim project comparateur1bit.circ as structural Verilog: 1 circuit, main circuit main
module main (
  input  R0,
  input  R1,
  output R0__R1,
  output R0___R1,
  output R0___R1_2
);

  wire and_3_out, and_4_out, not_1_out, not_2_out;

  not not_1 (not_1_out, R0);
  not not_2 (not_2_out, R1);
  and and_1 (R0__R1, R0, not_2_out);
  and and_2 (R0___R1, not_1_out, R1);
  and and_3 (and_3_out, R0, R1);
  and and_4 (and_4_out, not_1_out, not_2_out);
  or or_1 (R0___R1_2, and_3_out, and_4_out);
endmodule
