// Logisim project exo2.circ as structural Verilog: 1 circuit, main circuit main
module main (
  input  x,
  input  y,
  output S,
  output c
);

  xor xor_1 (S, x, y);
  and and_1 (c, y, x);
endmodule
