// Logisim project exo3.circ as structural Verilog: 1 circuit, main circuit main
module main (
  input  a,
  input  b,
  output D,
  output Bout
);

  wire not_1_out;

  not not_1 (not_1_out, a);
  xor xor_1 (D, a, b);
  and and_1 (Bout, b, not_1_out);
endmodule
