// Logisim project multiplexeur4vers1.circ as structural Verilog: 1 circuit, main circuit main
module main (
  input  E0,
  input  E1,
  input  E2,
  input  E3,
  input  a,
  input  b,
  output S
);

  wire and_1_out, and_2_out, and_3_out, and_4_out, not_1_out, not_2_out, not_3_out, not_4_out;

  not not_1 (not_1_out, a);
  not not_2 (not_2_out, b);
  not not_3 (not_3_out, b);
  not not_4 (not_4_out, a);
  and and_1 (and_1_out, not_1_out, E0, not_2_out);
  and and_2 (and_2_out, a, E1, not_3_out);
  and and_3 (and_3_out, not_4_out, E2, b);
  and and_4 (and_4_out, a, E3, b);
  or or_1 (S, and_1_out, and_2_out, and_3_out, and_4_out);
endmodule
